// Logisim project MultiCycle_CPU31.circ as structural Verilog: 6 circuits, main circuit CPU
module ALU_SBE (
  input  [7:0] A,
  input  [7:0] B,
  input  Asen,
  output [7:0] out_4
);

  wire [7:0] adder_1_out, subtractor_1_out;

  Adder adder_1 (.a(A), .b(B), .out(adder_1_out));  // open: cin, cout
  Subtractor subtractor_1 (.a(A), .b(B), .out(subtractor_1_out));  // open: bin, bout
  Multiplexer #(.width(8)) multiplexer_1 (
    .in0(adder_1_out), .in1(subtractor_1_out), .out(out_4), .sel(Asen), .en(1'b1));
endmodule

module BahaCrespo (
  input  Reset,
  input  Clock,
  input  R0_in,
  input  R1_in,
  input  R2_in,
  input  R3_in,
  input  R4_in,
  input  R5_in,
  input  R6_in,
  input  R7_in,
  input  [7:0] R0,
  input  [7:0] R1,
  input  [7:0] R2,
  input  [7:0] R4,
  input  [7:0] R5,
  input  [7:0] R6,
  input  [7:0] R7,
  input  [7:0] R3,
  output [7:0] R0_out,
  output [7:0] R1_out,
  output [7:0] R2_out,
  output [7:0] R3_out,
  output [7:0] R4_out,
  output [7:0] R5_out,
  output [7:0] R6_out,
  output [7:0] R7_out
);

  wire [7:0] undriven;

  Register register_1 (.D(R0), .en(R0_in), .Q(R0_out), .clk(Clock), .clr(Reset));
  Register register_2 (.D(R1), .en(R1_in), .Q(R1_out), .clk(Clock), .clr(Reset));
  Register register_3 (.D(R2), .en(R2_in), .Q(R2_out), .clk(Clock), .clr(Reset));
  Register register_4 (.D(undriven), .en(R3_in), .Q(R3_out), .clk(Clock), .clr(Reset));
  Register register_5 (.D(R4), .en(R4_in), .Q(R4_out), .clk(Clock), .clr(Reset));
  Register register_6 (.D(R5), .en(R5_in), .Q(R5_out), .clk(Clock), .clr(Reset));
  Register register_7 (.D(R6), .en(R6_in), .Q(R6_out), .clk(Clock), .clr(Reset));
  Register register_8 (.D(R7), .en(R7_in), .Q(R7_out), .clk(Clock), .clr(Reset));
endmodule

module _1_bit_ALU (
  input  in_1,
  input  in_2,
  input  in_3,
  input  in_4,
  input  in_5,
  output out_6,
  output out_7
);

  wire and_1_out, and_2_out, and_3_out, and_4_out, and_5_out, and_6_out, and_7_out, and_8_out, and_9_out,
       and_10_out, and_11_out, not_1_out, not_2_out, not_3_out, or_1_out, xor_1_out, xor_2_out;

  not not_1 (not_1_out, in_4);
  not not_2 (not_2_out, in_5);
  and and_1 (and_1_out, in_2, in_2);
  xor xor_1 (xor_1_out, in_2, in_2);
  and and_2 (and_2_out, not_1_out, not_2_out);
  and and_3 (and_3_out, not_2_out, in_4);
  and and_4 (and_4_out, not_1_out, in_5);
  and and_5 (and_5_out, in_5, in_4);
  not not_3 (not_3_out, in_1);
  or or_1 (or_1_out, in_1, in_2);
  and and_6 (and_6_out, in_1, in_2);
  and and_7 (and_7_out, xor_1_out, in_3);
  xor xor_2 (xor_2_out, in_3, xor_1_out);
  and and_8 (and_8_out, not_3_out, and_2_out);
  and and_9 (and_9_out, or_1_out, and_3_out);
  and and_10 (and_10_out, and_6_out, and_4_out);
  and and_11 (and_11_out, and_5_out, xor_2_out);
  or or_2 (out_7, and_7_out, and_1_out);
  ExactlyOne xor_3 (.out(out_6), .in0(and_8_out), .in1(and_9_out), .in2(and_10_out), .in3(and_11_out));
endmodule

module _2_bit_encounter (
  input  in_1,
  input  in_2,
  output out_3,
  output out_4
);

  wire and_1_out, and_2_out, Clock_out, not_1_out, or_1_out, t_ff_1_qn;

  Clock Clock (.out(Clock_out));
  not not_1 (not_1_out, in_1);
  T_Flip_Flop t_ff_1 (.clk(Clock_out), .T(in_2), .Q(out_3), .Qn(t_ff_1_qn));  // open: preset, reset, en
  and and_1 (and_1_out, not_1_out, out_3);
  and and_2 (and_2_out, t_ff_1_qn, in_1);
  or or_1 (or_1_out, and_1_out, and_2_out);
  T_Flip_Flop t_ff_2 (.clk(Clock_out), .T(or_1_out), .Q(out_4));  // open: Qn, preset, reset, en
endmodule

module CPU (
  input  [7:0] in_1,
  output Done,
  output Rx_in,
  output Rx_out,
  output Ry_out,
  output Ain,
  output Bin,
  output Bout,
  output Asen,
  output DINout,
  output I_Rin
);

  wire and_1_out, and_2_out, and_3_out, and_4_out, and_5_out, and_6_out, and_7_out, and_8_out, Clear_out,
       clock_1_out, d_ff_1_q, decoder_1_out0, decoder_1_out1, decoder_1_out2, decoder_1_out3, decoder_1_out4,
       decoder_1_out5, decoder_1_out6, decoder_1_out7, or_1_out, or_2_out, Reset_out;
  wire [1:0] Counter_2_q;
  wire [2:0] IR_q;
  wire [3:0] adder_1_out, adder_2_out, bahacrespo_1_r5_out, bahacrespo_1_r6_out, bahacrespo_1_r7_out,
       multiplexer_1_out;
  wire [7:0] A_q, alu_sbe_1_out_4, B_q, bahacrespo_1_r0_out, bahacrespo_1_r1_out, bahacrespo_1_r2_out,
       bahacrespo_1_r3_out, bahacrespo_1_r4_out, counter_1_q, multiplexer_3_out, ram_1_data;
  wire [7:3] IR_q_2;
  wire [7:4] bahacrespo_1_r5_out_2, bahacrespo_1_r6_out_2, bahacrespo_1_r7_out_2;

  Hex_Digit_Display hex_digit_display_1 (.value(bahacrespo_1_r7_out_2));  // open: dp
  Hex_Digit_Display hex_digit_display_2 (.value(bahacrespo_1_r7_out));  // open: dp
  Hex_Digit_Display hex_digit_display_3 (.value(bahacrespo_1_r6_out_2));  // open: dp
  Hex_Digit_Display hex_digit_display_4 (.value(bahacrespo_1_r6_out));  // open: dp
  Hex_Digit_Display hex_digit_display_5 (.value(bahacrespo_1_r5_out));  // open: dp
  Hex_Digit_Display hex_digit_display_6 (.value(bahacrespo_1_r5_out_2));  // open: dp
  Counter counter_1 (.Q(counter_1_q), .clk(clock_1_out), .clr(Clear_out));  // open: load, D, count, carry
  Button Clear (.out(Clear_out));
  Button Reset (.out(Reset_out));
  RAM ram_1 (.addr(counter_1_q), .data(ram_1_data), .clk(clock_1_out));  // open: sel, ld, clr
  Clock clock_1 (.out(clock_1_out));
  Adder #(.width(4)) adder_1 (.a(4'b0001), .b({1'b0, IR_q}), .out(adder_1_out));  // open: cin, cout
  Register IR (.D(ram_1_data), .en(I_Rin), .Q({IR_q_2, IR_q}), .clk(clock_1_out), .clr(Clear_out));
  Adder #(.width(4)) adder_2 (.a(4'b0001), .b({1'b0, IR_q_2[5:3]}), .out(adder_2_out));  // open: cin, cout
  BahaCrespo bahacrespo_1 (
    .R0(multiplexer_3_out), .R1(multiplexer_3_out), .R2(multiplexer_3_out), .R3(multiplexer_3_out),
    .R4(multiplexer_3_out), .R5(multiplexer_3_out), .R6(multiplexer_3_out), .R7(multiplexer_3_out),
    .Clock(clock_1_out), .R0_out(bahacrespo_1_r0_out), .R1_out(bahacrespo_1_r1_out),
    .R2_out(bahacrespo_1_r2_out), .R3_out(bahacrespo_1_r3_out), .R4_out(bahacrespo_1_r4_out),
    .R6_out({bahacrespo_1_r6_out_2, bahacrespo_1_r6_out}),
    .R7_out({bahacrespo_1_r7_out_2, bahacrespo_1_r7_out}), .R0_in(and_2_out), .R1_in(and_1_out),
    .R2_in(and_3_out), .R3_in(and_4_out), .R4_in(and_5_out), .R5_in(and_6_out), .R6_in(and_7_out),
    .R7_in(and_8_out), .R5_out({bahacrespo_1_r5_out_2, bahacrespo_1_r5_out}), .Reset(Reset_out));
  and and_1 (and_1_out, decoder_1_out1, Rx_in);
  and and_2 (and_2_out, decoder_1_out0, Rx_in);
  and and_3 (and_3_out, decoder_1_out2, Rx_in);
  and and_4 (and_4_out, decoder_1_out3, Rx_in);
  Decoder #(.select(3)) decoder_1 (
    .out0(decoder_1_out0), .out1(decoder_1_out1), .out2(decoder_1_out2), .out3(decoder_1_out3),
    .out4(decoder_1_out4), .out5(decoder_1_out5), .out6(decoder_1_out6), .out7(decoder_1_out7),
    .sel(IR_q_2[5:3]), .en(1'b1));
  Multiplexer #(.width(4)) multiplexer_1 (
    .in0(adder_1_out), .in1(adder_2_out), .out(multiplexer_1_out), .sel(Rx_out), .en(or_1_out));
  Multiplexer #(.width(4)) multiplexer_2 (
    .in0(4'b0000), .in1(4'b1001), .out(multiplexer_1_out), .sel(Bout), .en(or_2_out));
  Multiplexer #(.select(4), .width(8)) multiplexer_3 (
    .in0(ram_1_data), .in1(bahacrespo_1_r0_out), .in2(bahacrespo_1_r1_out), .in3(bahacrespo_1_r2_out),
    .in4(bahacrespo_1_r3_out), .in5(bahacrespo_1_r4_out), .in6({bahacrespo_1_r5_out_2, bahacrespo_1_r5_out}),
    .in7({bahacrespo_1_r6_out_2, bahacrespo_1_r6_out}), .in8({bahacrespo_1_r7_out_2, bahacrespo_1_r7_out}),
    .in9(B_q), .out(multiplexer_3_out), .sel(multiplexer_1_out));  // open: in10, in11, in12, in13, in14, in15, en
  and and_5 (and_5_out, decoder_1_out4, Rx_in);
  and and_6 (and_6_out, decoder_1_out5, Rx_in);
  or or_1 (or_1_out, Rx_out, Ry_out);
  Counter #(.width(2), .max('h3)) Counter_2 (
    .Q(Counter_2_q), .clk(clock_1_out), .clr(d_ff_1_q));  // open: load, D, count, carry
  and and_7 (and_7_out, decoder_1_out6, Rx_in);
  and and_8 (and_8_out, decoder_1_out7, Rx_in);
  or or_2 (or_2_out, Bout, DINout);
  Register A (.D(multiplexer_3_out), .en(Ain), .Q(A_q), .clk(clock_1_out));  // open: clr
  ALU_SBE alu_sbe_1 (.out_4(alu_sbe_1_out_4), .Asen(Asen), .A(A_q), .B(multiplexer_3_out));
  D_Flip_Flop d_ff_1 (.clk(clock_1_out), .D(Done), .Q(d_ff_1_q), .reset(Clear_out));  // open: Qn, preset, en
  Register B (.D(alu_sbe_1_out_4), .en(Bin), .Q(B_q), .clk(clock_1_out));  // open: clr
  ControlUnit controlunit_1 (
    .OP1(IR_q_2[7]), .OP0(IR_q_2[6]), .T1(Counter_2_q[1]), .T0(Counter_2_q[0]), .DONE(Done), .RX_in(Rx_in),
    .RX_out(Rx_out), .RY_out(Ry_out), .A_in(Ain), .B_in(Bin), .B_out(Bout), .ASEN(Asen), .DIN_out(DINout),
    .IR_in(I_Rin));
  Hex_Digit_Display hex_digit_display_7 (.value(in_1[7:4]));  // open: dp
  Hex_Digit_Display hex_digit_display_8 (.value(in_1[3:0]));  // open: dp

  // Notes on the sheet:
  //   RC = R7
  //   RB = R6
  //   RA = R5
  //   0YYY+1
  //   0XXX+1
endmodule

module ControlUnit (
  input  OP1,
  input  OP0,
  input  T1,
  input  T0,
  output DONE,
  output RX_in,
  output RX_out,
  output RY_out,
  output A_in,
  output B_in,
  output B_out,
  output ASEN,
  output DIN_out,
  output IR_in
);

  wire and_1_out, and_2_out, and_5_out, and_6_out, and_12_out, and_13_out, not_1_out, not_2_out, not_3_out,
       not_4_out, not_5_out, not_6_out, not_7_out, not_8_out, not_9_out, not_10_out, not_11_out, not_12_out;

  not not_1 (not_1_out, OP1);
  and and_1 (and_1_out, not_1_out, T0);
  and and_2 (and_2_out, T1, T0);
  not not_2 (not_2_out, T1);
  not not_3 (not_3_out, OP1);
  not not_4 (not_4_out, OP0);
  not not_5 (not_5_out, T0);
  not not_6 (not_6_out, T1);
  and and_3 (B_out, T1, T0);
  not not_7 (not_7_out, T0);
  not not_8 (not_8_out, OP1);
  not not_9 (not_9_out, T1);
  not not_10 (not_10_out, T0);
  or or_1 (DONE, and_1_out, and_2_out);
  not not_11 (not_11_out, OP1);
  and and_4 (RX_out, OP1, not_2_out, T0);
  and and_5 (and_5_out, not_3_out, not_4_out, T0);
  and and_6 (and_6_out, T1, not_5_out);
  and and_7 (A_in, OP1, not_6_out, T0);
  and and_8 (B_in, T1, not_12_out);
  not not_12 (not_12_out, T0);
  and and_9 (ASEN, OP0, T1, not_7_out);
  and and_10 (DIN_out, not_8_out, OP0, T0);
  and and_11 (IR_in, not_9_out, not_10_out);
  and and_12 (and_12_out, not_11_out, T0);
  and and_13 (and_13_out, T1, T0);
  or or_2 (RY_out, and_5_out, and_6_out);
  or or_3 (RX_in, and_12_out, and_13_out);
endmodule
